# Fritzing sketch led_running_light_circuit (saved by Fritzing 0.9.6b)
breadboards: 1

parts:
  LED1 = LED - 5mm [color="Red (633nm)" current=0.030 package="5 mm [THT]"]
  LED2 = LED - 5mm [color="Red (633nm)" current=0.030 package="5 mm [THT]"]
  LED3 = LED - 5mm [color="Red (633nm)" current=0.030 package="5 mm [THT]"]
  LED4 = LED - 5mm [color="Red (633nm)" current=0.030 package="5 mm [THT]"]
  LED5 = LED - 5mm [color="Red (633nm)" current=0.030 package="5 mm [THT]"]
  LED6 = LED - 5mm [color="Red (633nm)" current=0.030 package="5 mm [THT]"]
  LED7 = LED - 5mm [color="Red (633nm)" current=0.030 package="5 mm [THT]"]
  LED8 = LED - 5mm [color="Red (633nm)" current=0.030 package="5 mm [THT]"]
  R1 = Resistor [tolerance=±5% power=0.25 resistance=15 package=THT]
  R2 = Resistor [tolerance=±5% power=0.25 resistance=15 package=THT]
  R3 = Resistor [tolerance=±5% power=0.25 resistance=15 package=THT]
  R4 = Resistor [tolerance=±5% power=0.25 resistance=15 package=THT]
  R5 = Resistor [tolerance=±5% power=0.25 resistance=15 package=THT]
  R6 = Resistor [tolerance=±5% power=0.25 resistance=15 package=THT]
  R7 = Resistor [tolerance=±5% power=0.25 resistance=15 package=THT]
  R8 = Resistor [tolerance=±5% power=0.25 resistance=15 package=THT]
  S1 = Momentary Switch [package=ksa_sealed_tac_switch]
  S2 = Momentary Switch [package=ksa_sealed_tac_switch]
  J1 = STM32 Nucleo boards
  C1 = Ceramic Capacitor [capacitance=100nF voltage=35V package="100 mil [THT, multilayer]"]
  U2 = 74HC595 [package="DIP16 [THT]"]
  U4 = JOYSTICK-PSP1000 [package=joystick-psp1000]
  LED9 = LED - 5mm [color="Green (570nm)" current=0.030 package="5 mm [THT]"]
  R9 = Resistor [tolerance=±5% power=0.25 resistance=15 package=THT]
  LED10 = LED - 5mm [color="Red (633nm)" current=0.030 package="5 mm [THT]"]
  R10 = Resistor [tolerance=±5% power=0.25 resistance=15 package=THT]
  R11 = Resistor [tolerance=±5% power=0.25 resistance=15 package=THT]
  LED11 = LED - 5mm [color="Orange (620nm)" current=0.030 package="5 mm [THT]"]

nets:
  GND: LED1.cathode, LED2.cathode, LED3.cathode, LED4.cathode, LED5.cathode, LED6.cathode, LED7.cathode, LED8.cathode, J1.GND#229, C1.0, U2.GND, U2.OE, LED9.cathode, LED10.cathode, LED11.cathode
  N1: LED1.anode, R8.Pin_0
  N2: LED2.anode, R7.Pin_0
  N3: LED3.anode, R6.Pin_0
  N4: LED4.anode, R5.Pin_0
  N5: LED5.anode, R4.Pin_0
  N6: LED6.anode, R3.Pin_0
  N7: LED7.anode, R2.Pin_0
  N8: LED8.anode, R1.Pin_0
  N9: R1.Pin_1, U2.Q7
  N10: R2.Pin_1, U2.Q6
  N11: R3.Pin_1, U2.Q5
  N12: R4.Pin_1, U2.Q4
  N13: R5.Pin_1, U2.Q3
  N14: R6.Pin_1, U2.Q2
  N15: R7.Pin_1, U2.Q1
  N16: R8.Pin_1, U2.Q0
  N17: S1.1, S1.2
  N18: S1.3, S1.4
  N19: S2.1, S2.2
  N20: S2.3, S2.4
  N21: J1.PC5, R9.Pin_1
  3.3V: J1.3V3, C1.1, U2.MR, U2.VCC, U4.VCC
  N22: J1.PA6, R11.Pin_1
  N23: J1.PA7, R10.Pin_1
  N24: J1.PA4, U4.X
  N25: J1.PC0, U4.Y
  N26: J1.PC10, U2.SH_CP
  N27: J1.PC12, U2.DS
  N28: J1.PA15, U2.ST_CP
  N29: J1.GND#3328, U4.GND
  N30: LED9.anode, R9.Pin_0
  N31: LED10.anode, R10.Pin_0
  N32: R11.Pin_0, LED11.anode

notes:
  LED Strip with red LEDs
  choose LED strip program
  choose LED blinking rate
  Green LED 1: LED Strip is blinking
  Yellow LED 1: Joystick Y
  Red LED 1: Joystick X
  R LED 1
  Y LED 1
  G LED 1
  3 x 150 Ohm
  8 x 150 Ohm
  Dim the LEDs:
  X > Red LED 1
  Y > Yellow LED 1
  SPI MOSI
  SPI ENA
  SPI SCK
